// Logisim project smips.circ as structural Verilog: 9 circuits, main circuit Board
module Board (
);

  wire CLK, HALT, MEM_WE, RESET, TTY_WE;
  wire [3:0] MEM_BE;
  wire [6:0] TTY_DATA;
  wire [31:0] MEM_ADDR, MEM_RDATA, MEM_WDATA;

  Clock Reloj (.out(CLK));
  Button u_Reset (.out(RESET));
  CPU cpu_1 (
    .CLK(CLK), .RESET(RESET), .MEM_RDATA(MEM_RDATA), .MEM_ADDR(MEM_ADDR), .MEM_WDATA(MEM_WDATA),
    .MEM_BE(MEM_BE), .MEM_WE(MEM_WE), .TTY_DATA(TTY_DATA), .TTY_WE(TTY_WE), .HALT(HALT));
  TTY #(.cols(48), .rows(12)) tty_1 (.data(TTY_DATA), .clk(CLK), .we(TTY_WE), .clr(RESET));
  Memory memory_1 (.CLK(CLK), .ADDR(MEM_ADDR), .WDATA(MEM_WDATA), .BE(MEM_BE), .WE(MEM_WE), .RDATA(MEM_RDATA));
  LED u_Halt (.in(HALT));

  // Notes on the sheet:
  //   S-MIPS | Board
  //   No modificar: la CPU se implementa dentro del subcircuito CPU.
endmodule

module CPU (
  input  CLK,
  input  RESET,
  input  [31:0] MEM_RDATA,
  output [31:0] MEM_ADDR,
  output [31:0] MEM_WDATA,
  output [3:0] MEM_BE,
  output MEM_WE,
  output [6:0] TTY_DATA,
  output TTY_WE,
  output HALT
);


  // Notes on the sheet:
  //   CPU S-MIPS: implementar aqui
  //   No cambiar nombres, anchos ni sentido de los pines: la placa depende de ellos.
endmodule

module Memory (
  input  CLK,
  input  [31:0] ADDR,
  input  [31:0] WDATA,
  input  [3:0] BE,
  input  WE,
  output [31:0] RDATA
);

  RAM #(.addrWidth(12), .asyncread("true"), .byteenables("byteEnables"), .dataWidth(32), .\type ("nonvolatile")) Main_Memory (
    .addr(ADDR[13:2]), .we(WE), .oe(1'b1), .clk(CLK), .din(WDATA), .dout(RDATA), .be3(BE[3]), .be2(BE[2]),
    .be1(BE[1]), .be0(BE[0]));

  // Other names for the same wires on the sheet: A[11:0] = ADDR[13:2]

  // Notes on the sheet:
  //   Memoria unificada: 4096 palabras de 32 bits (16 KiB), little-endian
  //   Lectura combinacional; escritura en el flanco de subida de CLK con WE=1, solo en los bytes con BE=1.
  //   Se usan los bits 13..2 de ADDR; los demas se ignoran (el espacio se repite cada 16 KiB).
endmodule

module Datapath (
);

  wire ALU_sA, Branch_Take, Illegal, Syscall, WA, WB, WResult, zero;
  wire [1:0] ALU_sB, Branch_Type, Imm_Type, Jump_Type;
  wire [2:0] ALU_Op, Instr_Type, undriven;
  wire [31:0] A, ALU_Out, B, bit_extender_1_out, bit_extender_2_out, Imm_32, Input_A, Input_B, IR, MDR, PC,
       RA, RB, Result, shifter_1_out;

  Register #(.width(32)) u_PC (.Q(PC));  // open: D, en, clk, clr
  Register #(.width(32)) u_A (.D(RA), .en(WA), .Q(A));  // open: clk, clr
  Register #(.width(32)) u_ALU_Out (.D(Result), .en(WResult), .Q(ALU_Out));  // open: clk, clr
  Register #(.width(32)) u_IR (.Q(IR));  // open: D, en, clk, clr
  Register #(.width(32)) u_B (.D(RB), .en(WB), .Q(B));  // open: clk, clr
  Instruction_Decoder instruction_decoder_1 (
    .Outputs(Instr_Type), .out_4(ALU_Op), .out_5(Branch_Type), .out_6(Jump_Type), .out_7(Imm_Type),
    .out_8(Syscall), .out_9(Illegal));  // open: Inputs, in_2
  assign bit_extender_1_out = {{16{1'b0}}, IR[15:0]};  // Bit_Extender bit_extender_1
  assign bit_extender_2_out = {{16{IR[15]}}, IR[15:0]};  // Bit_Extender bit_extender_2
  Shifter #(.width(32)) shifter_1 (.in(Imm_32), .\dist (5'b00010), .out(shifter_1_out));
  Multiplexer #(.width(32)) multiplexer_1 (.in0(PC), .in1(A), .out(Input_A), .sel(ALU_sA));
  Multiplexer #(.select(2), .width(32)) multiplexer_2 (
    .in1(bit_extender_1_out), .in2({IR[15:0], {16{1'b0}}}), .in3(bit_extender_2_out), .out(Imm_32),
    .sel(Imm_Type));  // open: in0
  Multiplexer #(.select(2), .width(32)) multiplexer_3 (
    .in0(B), .in1(32'h4), .in2(Imm_32), .in3(shifter_1_out), .out(Input_B), .sel(ALU_sB));
  Register #(.width(32)) u_MDR (.Q(MDR));  // open: D, en, clk, clr
  Branch_Control branch_control_1 (.in_1(Branch_Type), .in_2(zero), .out_3(Branch_Take));
  Register_File register_file_1 (
    .in_2(IR[25:21]), .in_3(IR[20:16]), .out_8(RA), .out_9(RB));  // open: in_1, in_4, in_5, in_6, in_7
  ALU alu_1 (.in_1(Input_A), .in_2(Input_B), .in_3(undriven), .out_4(Result), .out_5(zero));

  // Notes on the sheet:
  //   Registers A, B, ALU_Result
  //   ALU_Inputs
  //   Imm_Extnder
  //   Register File | ALU
endmodule

module ALU (
  input  [31:0] in_1,
  input  [31:0] in_2,
  input  [2:0] in_3,
  output [31:0] out_4,
  output out_5
);

  wire comparator_1_lt;
  wire [31:0] add, and_r, or_r, sll_r, slr_r, slt_r, sub;

  Adder #(.width(32)) adder_1 (.a(in_1), .b(in_2), .out(add));  // open: cin, cout
  Subtractor #(.width(32)) subtractor_1 (.a(in_1), .b(in_2), .out(sub));  // open: bin, bout
  Shifter #(.shift("lr"), .width(32)) shifter_1 (.in(in_1), .\dist (in_2[4:0]), .out(slr_r));
  Shifter #(.width(32)) shifter_2 (.in(in_1), .\dist (in_2[4:0]), .out(sll_r));
  assign and_r = in_1 & in_2;  // AND_Gate and_1, 32 bits wide
  assign or_r = in_1 | in_2;  // OR_Gate or_1, 32 bits wide
  Comparator #(.width(32)) comparator_1 (.a(in_1), .b(in_2), .lt(comparator_1_lt));  // open: gt, eq
  assign slt_r = {{31{comparator_1_lt}}, comparator_1_lt};  // Bit_Extender bit_extender_1
  Multiplexer #(.select(3), .width(32)) multiplexer_1 (
    .in0(add), .in1(sub), .in2(and_r), .in3(or_r), .in4(slt_r), .in5(sll_r), .in6(slr_r), .out(out_4),
    .sel(in_3));  // open: in7
  Comparator #(.width(32)) comparator_2 (.a({32{1'b0}}), .b(out_4), .eq(out_5));  // open: gt, lt

  // Other names for the same wires on the sheet: Rd[31:0] = out_4; Rs[31:0] = in_1; Rt[31:0] = in_2;
  //   Selector_ALU[2:0] = in_3; zero = out_5

  // Notes on the sheet:
  //   Inputs
  //   Outputs
  //   ALU
  //   add -> 000
  //   sub -> 001
  //   and -> 010
  //   or -> 011
  //   slt -> 100
  //   sll -> 101
  //   slr -> 110
endmodule

module Register_File (
  input  [31:0] in_1,
  input  [4:0] in_2,
  input  [4:0] in_3,
  input  [4:0] in_4,
  input  in_5,
  input  in_6,
  input  in_7,
  output [31:0] out_8,
  output [31:0] out_9
);

  wire En01, En02, En03, En04, En05, En06, En07, En08, En09, En10, En11, En12, En13, En14, En15, En16, En17,
       En18, En19, En20, En21, En22, En23, En24, En25, En26, En27, En28, En29, En30, En31;
  wire [31:0] gp_28, RR00, RR01, RR02, RR03, RR04, RR05, RR06, RR07, RR08, RR09, RR10, RR11, RR12, RR13,
       RR14, RR15, RR16, RR17, RR18, RR19, RR20, RR21, RR22, RR23, RR24, RR25, RR26, RR27, RR28, RR29, RR30,
       RR31, sp_29;

  Register #(.width(32)) register_1 (.clk(in_5), .Q(RR00));  // open: D, en, clr
  Register #(.width(32)) register_2 (.D(in_1), .en(En01), .clk(in_5), .Q(RR01), .clr(in_7));
  Register #(.width(32)) register_3 (.D(in_1), .en(En02), .clk(in_5), .Q(RR02), .clr(in_7));
  Register #(.width(32)) register_4 (.D(in_1), .en(En03), .clk(in_5), .Q(RR03), .clr(in_7));
  Register #(.width(32)) register_5 (.D(in_1), .en(En04), .clk(in_5), .Q(RR04), .clr(in_7));
  Register #(.width(32)) register_6 (.D(in_1), .en(En05), .clk(in_5), .Q(RR05), .clr(in_7));
  Register #(.width(32)) register_7 (.D(in_1), .en(En06), .clk(in_5), .Q(RR06), .clr(in_7));
  Register #(.width(32)) register_8 (.D(in_1), .en(En07), .clk(in_5), .Q(RR07), .clr(in_7));
  Register #(.width(32)) register_9 (.D(in_1), .en(En08), .clk(in_5), .Q(RR08), .clr(in_7));
  Register #(.width(32)) register_10 (.D(in_1), .en(En09), .clk(in_5), .Q(RR09), .clr(in_7));
  Register #(.width(32)) register_11 (.D(in_1), .en(En10), .clk(in_5), .Q(RR10), .clr(in_7));
  Register #(.width(32)) register_12 (.D(in_1), .en(En11), .clk(in_5), .Q(RR11), .clr(in_7));
  Demultiplexer #(.disabled("Z"), .select(5)) demultiplexer_1 (
    .out1(En01), .out2(En02), .out3(En03), .out4(En04), .out5(En05), .out6(En06), .out7(En07), .out8(En08),
    .out9(En09), .out10(En10), .out11(En11), .out12(En12), .out13(En13), .out14(En14), .out15(En15),
    .out16(En16), .out17(En17), .out18(En18), .out19(En19), .out20(En20), .out21(En21), .out22(En22),
    .out23(En23), .out24(En24), .out25(En25), .out26(En26), .out27(En27), .out28(En28), .out29(En29),
    .out30(En30), .out31(En31), .in(in_6), .sel(in_4));  // open: out0
  Register #(.width(32)) register_13 (.D(in_1), .en(En12), .clk(in_5), .Q(RR12), .clr(in_7));
  Register #(.width(32)) register_14 (.D(in_1), .en(En13), .clk(in_5), .Q(RR13), .clr(in_7));
  Register #(.width(32)) register_15 (.D(in_1), .en(En14), .clk(in_5), .Q(RR14), .clr(in_7));
  Register #(.width(32)) register_16 (.D(in_1), .en(En15), .clk(in_5), .Q(RR15), .clr(in_7));
  Register #(.width(32)) register_17 (.D(in_1), .en(En16), .clk(in_5), .Q(RR16), .clr(in_7));
  Register #(.width(32)) register_18 (.D(in_1), .en(En17), .clk(in_5), .Q(RR17), .clr(in_7));
  Multiplexer #(.select(5), .width(32)) multiplexer_1 (
    .in0(RR00), .in1(RR01), .in2(RR02), .in3(RR03), .in4(RR04), .in5(RR05), .in6(RR06), .in7(RR07),
    .in8(RR08), .in9(RR09), .in10(RR10), .in11(RR11), .in12(RR12), .in13(RR13), .in14(RR14), .in15(RR15),
    .in16(RR16), .in17(RR17), .in18(RR18), .in19(RR19), .in20(RR20), .in21(RR21), .in22(RR22), .in23(RR23),
    .in24(RR24), .in25(RR25), .in26(RR26), .in27(RR27), .in28(RR28), .in29(RR29), .in30(RR30), .in31(RR31),
    .out(out_8), .sel(in_2));
  Register #(.width(32)) register_19 (.D(in_1), .en(En18), .clk(in_5), .Q(RR18), .clr(in_7));
  Register #(.width(32)) register_20 (.D(in_1), .en(En19), .clk(in_5), .Q(RR19), .clr(in_7));
  Register #(.width(32)) register_21 (.D(in_1), .en(En20), .clk(in_5), .Q(RR20), .clr(in_7));
  Register #(.width(32)) register_22 (.D(in_1), .en(En21), .clk(in_5), .Q(RR21), .clr(in_7));
  Register #(.width(32)) register_23 (.D(in_1), .en(En22), .clk(in_5), .Q(RR22), .clr(in_7));
  Register #(.width(32)) register_24 (.D(in_1), .en(En23), .clk(in_5), .Q(RR23), .clr(in_7));
  Multiplexer #(.select(5), .width(32)) multiplexer_2 (
    .in0(RR00), .in1(RR01), .in2(RR02), .in3(RR03), .in4(RR04), .in5(RR05), .in6(RR06), .in7(RR07),
    .in8(RR08), .in9(RR09), .in10(RR10), .in11(RR11), .in12(RR12), .in13(RR13), .in14(RR14), .in15(RR15),
    .in16(RR16), .in17(RR17), .in18(RR18), .in19(RR19), .in20(RR20), .in21(RR21), .in22(RR22), .in23(RR23),
    .in24(RR24), .in25(RR25), .in26(RR26), .in27(RR27), .in28(RR28), .in29(RR29), .in30(RR30), .in31(RR31),
    .out(out_9), .sel(in_3));
  Register #(.width(32)) register_25 (.D(in_1), .en(En24), .clk(in_5), .Q(RR24), .clr(in_7));
  Register #(.width(32)) register_26 (.D(in_1), .en(En25), .clk(in_5), .Q(RR25), .clr(in_7));
  Register #(.width(32)) register_27 (.D(in_1), .en(En26), .clk(in_5), .Q(RR26), .clr(in_7));
  Register #(.width(32)) register_28 (.D(in_1), .en(En27), .clk(in_5), .Q(RR27), .clr(in_7));
  Register #(.width(32)) register_29 (.D(gp_28), .en(En28), .clk(in_5), .Q(RR28));  // open: clr
  Register #(.width(32)) register_30 (.D(sp_29), .en(En29), .clk(in_5), .Q(RR29));  // open: clr
  Register #(.width(32)) register_31 (.D(in_1), .en(En30), .clk(in_5), .Q(RR30), .clr(in_7));
  Register #(.width(32)) register_32 (.D(in_1), .en(En31), .clk(in_5), .Q(RR31), .clr(in_7));
  Multiplexer #(.width(32)) multiplexer_3 (.in0(in_1), .in1(32'h1800), .out(gp_28), .sel(in_7));
  Multiplexer #(.width(32)) multiplexer_4 (.in0(in_1), .in1(32'h3ffc), .out(sp_29), .sel(in_7));

  // Other names for the same wires on the sheet: A[31:0] = out_8; B[31:0] = out_9; clk = in_5; Data[31:0] = in_1;
  //   R_W = in_6; reset = in_7; SelectorA[4:0] = in_2; SelectorB[4:0] = in_3; SelectorReg[4:0] = in_4

  // Notes on the sheet:
  //   Inputs
  //   Registers
  //   Selector Data
  //   Selector A
  //   Selector B
  //   Outputs
  //   Registers 28, 29
endmodule

module Instruction_Decoder (
  input  [5:0] Inputs,
  input  [5:0] in_2,
  output [2:0] Outputs,
  output [2:0] out_4,
  output [1:0] out_5,
  output [1:0] out_6,
  output [1:0] out_7,
  output out_8,
  output out_9
);

  wire BRANCH, fh_0, fh_1, fh_2, fh_3, fh_4, fh_5, fh_6, fh_7, fl_0, fl_1, fl_2, fl_3, fl_4, fl_5, fl_6,
       fl_7, I, IMM, is_add, is_addi, is_addiu, is_addu, is_and, is_andi, is_j, is_jal, is_jr, is_lb, is_lbu,
       is_lui, is_lw, is_or, is_ori, is_sb, is_sll, is_slt, is_slti, is_srl, is_sub, is_sw, J, JUMP, LOAD,
       oh_0, oh_1, oh_2, oh_3, oh_4, oh_5, oh_6, oh_7, ol_0, ol_1, ol_2, ol_3, ol_4, ol_5, ol_6, ol_7,
       or_14_out, or_18_out, R, R_Type, STORE;

  and and_1 (R_Type, ol_0, oh_0);
  and and_2 (is_j, ol_2, oh_0);
  and and_3 (is_jal, ol_3, oh_0);
  and and_4 (out_5[0], ol_4, oh_0);
  and and_5 (out_5[1], ol_5, oh_0);
  and and_6 (is_addi, ol_0, oh_1);
  Decoder #(.enable("false"), .select(3)) decoder_1 (
    .out0(ol_0), .out1(ol_1), .out2(ol_2), .out3(ol_3), .out4(ol_4), .out5(ol_5), .out6(ol_6), .out7(ol_7),
    .sel(Inputs[2:0]));
  Decoder #(.enable("false"), .select(3)) decoder_2 (
    .out0(fl_0), .out1(fl_1), .out2(fl_2), .out3(fl_3), .out4(fl_4), .out5(fl_5), .out6(fl_6), .out7(fl_7),
    .sel(in_2[2:0]));
  and and_7 (is_addiu, ol_1, oh_1);
  and and_8 (is_slti, ol_2, oh_1);
  and and_9 (is_andi, ol_4, oh_1);
  Decoder #(.enable("false"), .select(3)) decoder_3 (
    .out0(oh_0), .out1(oh_1), .out2(oh_2), .out3(oh_3), .out4(oh_4), .out5(oh_5), .out6(oh_6), .out7(oh_7),
    .sel(Inputs[5:3]));
  Decoder #(.enable("false"), .select(3)) decoder_4 (
    .out0(fh_0), .out1(fh_1), .out2(fh_2), .out3(fh_3), .out4(fh_4), .out5(fh_5), .out6(fh_6), .out7(fh_7),
    .sel(in_2[5:3]));
  and and_10 (is_add, R_Type, fl_0, fh_4);
  and and_11 (is_sub, R_Type, fl_2, fh_4);
  and and_12 (is_and, R_Type, fl_4, fh_4);
  and and_13 (is_or, R_Type, fl_5, fh_4);
  and and_14 (is_ori, ol_5, oh_1);
  and and_15 (is_lui, ol_7, oh_1);
  and and_16 (is_lb, ol_0, oh_4);
  and and_17 (is_sll, R_Type, fl_0, fh_0);
  and and_18 (is_srl, R_Type, fl_2, fh_0);
  and and_19 (is_slt, R_Type, fl_2, fh_5);
  and and_20 (is_addu, R_Type, fl_1, fh_4);
  and and_21 (is_lw, ol_3, oh_4);
  and and_22 (is_lbu, ol_4, oh_4);
  and and_23 (is_sb, ol_0, oh_5);
  and and_24 (out_8, R_Type, fl_0, fh_1);
  and and_25 (is_jr, R_Type, fl_1, fh_1);
  and and_26 (is_sw, ol_3, oh_5);
  nor nor_1 (out_9, R, I, J);
  or or_1 (J, is_j, is_jal);
  or or_2 (out_4[0], is_sub, out_5[0], out_5[1], is_or, is_ori, is_sll);
  or or_3 (out_4[1], is_and, is_andi, is_or, is_ori, is_srl);
  or or_4 (out_4[2], is_slt, is_slti, is_sll, is_srl);
  or or_5 (R, is_add, is_sub, is_and, is_or, is_sll, is_srl, is_slt, is_addu, out_8, is_jr);
  or or_6 (STORE, is_sb, is_sw);
  or or_7 (JUMP, is_j, is_jal);
  or or_8 (LOAD, is_lw, is_lb, is_lbu);
  or or_9 (BRANCH, out_5[0], out_5[1]);
  or or_10 (IMM, is_addi, is_addiu, is_andi, is_ori, is_slti, is_lui);
  or or_11 (I, out_5[0], out_5[1], is_addi, is_addiu, is_slti, is_andi, is_ori, is_lui, is_lb, is_lw, is_sb, is_sw, is_lbu);
  or or_12 (out_6[0], is_j, is_jr);
  or or_13 (out_6[1], is_jr, is_jal);
  or or_14 (or_14_out, is_andi, is_ori);
  or or_15 (Outputs[0], IMM, STORE, JUMP, out_9);
  or or_16 (Outputs[1], LOAD, STORE);
  or or_17 (Outputs[2], BRANCH, JUMP, out_8, out_9);
  or or_18 (or_18_out, is_addi, is_addiu, is_slti, is_lw, is_sw, is_lb, is_lbu, is_sb, out_5[0], out_5[1]);
  or or_19 (out_7[0], or_14_out, or_18_out);
  or or_20 (out_7[1], or_18_out, is_lui);

  // Other names for the same wires on the sheet: ALU_Op[2:0] = out_4; Branch_Type[1:0] = out_5; is_beq = out_5[0];
  //   is_bne = out_5[1]; FL[2:0] = in_2[2:0]; funct[5:0] = in_2; FH[2:0] = in_2[5:3]; ILLEGAL = out_9;
  //   Imm_Type[1:0] = out_7; Instr_Type[2:0] = Outputs; is_syscall = out_8; Syscall = out_8; Jump_Type[1:0] = out_6;
  //   OL[2:0] = Inputs[2:0]; op[5:0] = Inputs; OH[2:0] = Inputs[5:3]

  // Notes on the sheet:
  //   Codification_R
  //   Codification_J
  //   Codification_I
  //   Decoders
  //   Codification_Outputs
endmodule

module Branch_Control (
  input  [1:0] in_1,
  input  in_2,
  output out_3
);

  wire and_1_out, and_2_out, and_3_out, and_4_out;

  and and_1 (and_1_out, in_1[0], ~in_1[1]);  // AND_Gate
  and and_2 (and_2_out, in_1[1], ~in_1[0]);  // AND_Gate
  and and_3 (and_3_out, and_1_out, in_2);
  and and_4 (and_4_out, ~in_2, and_2_out);  // AND_Gate
  or or_1 (out_3, and_3_out, and_4_out);

  // Other names for the same wires on the sheet: Branch_Take = out_3; Branch_Type[1:0] = in_1; Zero = in_2

  // Notes on the sheet:
  //   Inputs
  //   Outputs
  //   01 -> beq
  //   10 -> bne
  //   00 -> no hay branch
endmodule

module Control_Unit (
  input  Inputs,
  input  in_2,
  input  [2:0] in_3,
  input  [1:0] in_4,
  input  [1:0] in_5,
  input  in_6,
  output Outputs,
  output out_8,
  output out_9,
  output out_10,
  output out_11,
  output out_12,
  output out_13,
  output out_14,
  output [1:0] out_15,
  output out_16,
  output out_17
);

  wire Branch, Illegal, Imm, is_decode_illegal, is_decode_RType, Jump, Load, R_Type, Store, Syscall;
  wire [1:0] Next_State;
  wire [3:0] Current_State;

  Register #(.width(4)) State (.D({{2{out_17}}, Next_State}), .clk(Inputs), .Q(Current_State), .clr(in_2));  // open: en
  or or_1 (out_14, out_8, out_11);
  not not_1 (out_15[1], out_11);
  Decoder #(.enable("false"), .select(3)) decoder_1 (
    .out0(R_Type), .out1(Imm), .out2(Load), .out3(Store), .out4(Branch), .out5(Jump), .out6(Syscall),
    .out7(Illegal), .sel(in_3));
  or or_2 (Next_State[0], is_decode_RType, out_13, out_17);
  or or_3 (Next_State[1], out_11, out_13, out_17);
  Comparator #(.mode("unsigned"), .width(4)) comparator_1 (.a(Current_State), .b(4'b0000), .eq(out_8));  // open: gt, lt
  Comparator #(.mode("unsigned"), .width(4)) comparator_2 (.a(Current_State), .b(4'b0001), .eq(out_9));  // open: gt, lt
  Comparator #(.mode("unsigned"), .width(4)) comparator_3 (
    .a(Current_State), .b(4'b0010), .eq(out_11));  // open: gt, lt
  Comparator #(.mode("unsigned"), .width(4)) comparator_4 (
    .a(Current_State), .b(4'b0011), .eq(out_13));  // open: gt, lt
  Comparator #(.mode("unsigned"), .width(4)) comparator_5 (
    .a(Current_State), .b(4'b1111), .eq(out_17));  // open: gt, lt
  and and_1 (is_decode_illegal, out_9, Illegal);
  and and_2 (is_decode_RType, out_9, R_Type);

  assign out_10 = out_9;
  assign out_15[0] = out_15[1];
  assign Outputs = out_8;

  // Other names for the same wires on the sheet: Branch_Type[1:0] = in_4; clk = Inputs; Instr_Type[2:0] = in_3;
  //   A_w = out_9; B_w = out_9; is_decode = out_9; ALUout_w = out_11; is_execR = out_11; IR_w = out_8;
  //   is_fetch = out_8; PC_w = out_8; is_wbR = out_13; R_W = out_13; Jump_Type[1:0] = in_5; MDR_w = out_12;
  //   Halt = out_17; is_halt = out_17; Next_State[3:2] = {2{out_17}}; PC_r = out_16; reset = in_2; S_A = out_14;
  //   S_B[1:0] = {2{out_15[1]}}; zero = in_6

  // Notes on the sheet:
  //   Codificacion de Estados
  //   0000 FETCH
  //   0001 DECODE
  //   0010 EXEC_RTYPE
  //   0011 WB_RTYPE
  //   1111 HALT
  //   Registro de Estado
  //   Codificacion de Salidas
  //   Obtener tipo
  //   de instruccion
  //   Actualizar Estado
  //   Pendiente...
  //   Analizar Estado Actual
endmodule
